# Fritzing sketch pico_player_hackathon (saved by Fritzing 1.0.4)
breadboards: 1

parts:
  Pico_H1 = Raspberry Pi Pico H
  Buzzer = Piezo Buzzer
  S1 = Pushbutton [package="[THT]"]
  LED1 = RGB LED PL9823 F5 [package="5 mm [THT]"]
  LED2 = RGB LED PL9823 F5 [package="5 mm [THT]"]

nets:
  VDD: Pico_H1.VBUS, LED1.VDD, LED2.VDD
  GND: Pico_H1.GND, Buzzer.pin_1, S1.Pin_3, S1.Pin_4, LED1.GND, LED2.DO
  N1: Pico_H1.GP17, S1.Pin_1, S1.Pin_2
  N2: Pico_H1.GP16, Buzzer.pin_2
  N3: Pico_H1.GP15, LED1.DIN
  N4: LED1.DO, LED2.DIN

notes:
  5v Rail
  3.3V Rail
  LED Data
  Buzzer PWM
  Voltage (+)
  Button Input
  Ground

custom parts:
  Raspberry Pi Pico H: Raspberry Pi Pico H. Based around the RP2040 microcontroller the Pico H is a low cost microcontroller device bringing Raspberry Pi quality, cost, and easy of use to the microcontroller space.
  Piezo Buzzer: Part from https://www.nutsvolts.com/magazine/article/november2012_SmileysWorkshop. Breadboard and icon images modified to be 0.3" in spacing and be more similar to the actual physical part.
  RGB LED PL9823 F5: A 5mm tri-color LED with red, green and blue inside. this led includes WS2811 controller.
